# Fritzing sketch Gun (saved by Fritzing 0.9.2b)
circuit board: 4.34376cm x 3.95149cm
breadboards: 1

parts:
  R1 = Resistor [tolerance=±5% resistance=220 package=THT]
  J2 = female pin header, 2 pins [form="♀ (female)"]
  R2 = Resistor [tolerance=±5% resistance=220 package=THT]
  J3 = female pin header, 2 pins [form="♀ (female)"]
  R3 = Resistor [tolerance=±5% resistance=220 package=THT]
  J4 = female pin header, 2 pins [form="♀ (female)"]
  R4 = Resistor [tolerance=±5% resistance=220 package=THT]
  J5 = double row female pin header, 8 pins [form="♀ (female)"]
  J1 = female pin header, 2 pins [form="♀ (female)"]
  Part1 = Arduino Pro Mini v13
  Q2 = NPN-Transistor [package="TO92 [THT]"]
  VCC1 = Battery block 9V
  Q3 = NPN-Transistor [package="TO92 [THT]"]
  C1 = Ceramic Capacitor [capacitance=100nF package="100 mil [THT, multilayer]"]
  C2 = Electrolytic Capacitor [capacitance=1µF package="100 mil [THT, electrolytic]"]

nets:
  GND: R1.Pin_0, J2.pin2, J3.pin2, J4.pin2, J5.pin1, Part1.GND, Q2.E, VCC1.-, Q3.B, C1.1, C2.-
  N1: R1.Pin_1, Part1.D3_PWM, Q2.B
  N2: J2.pin1, R2.Pin_1, Part1.D4
  5V: R2.Pin_0, R3.Pin_0, R4.Pin_0, Part1.VCC, Q3.C, C1.0
  N3: J3.pin1, R3.Pin_1, Part1.D5_PWM
  N4: J4.pin1, R4.Pin_1, Part1.D6_PWM
  N5: J5.pin2, Part1.D9_PWM
  N6: J5.pin3, Part1.D13/SCK
  N7: J5.pin4, Part1.D12/MISO
  N8: J5.pin6, Part1.D11_PWM/MOSI
  N9: J5.pin7, Part1.D10_PWM/SS
  N10: J5.pin8, Q3.E, C2.+
  N11: J1.pin1, Part1.RAW, VCC1.+
  N12: J1.pin2, Q2.C

// code stored in the sketch: Gun.ino

